// Logisim project RISC_processor.circ as structural Verilog: 14 circuits, main circuit main
// ALUout
module main (
  input  reset
);

  wire add, addi, ALUinB, \and , and_2_out, and_3_out, beq, bgt, clk, DMwe, eq, gt, \input , j, jal, jPCL,
       jr, key_re, keyboard_1_avail, lw, memory_latch_1_oe_latched, memory_latch_1_we_latched, not_1_out,
       not_2_out, not_3_out, not_4_out, \or , or_2_out, \output , Rdst, Rwd, Rwe, shiftlft, shiftrt, sub, sw,
       tty_we;
  wire [2:0] ALUop, multiplexer_1_out, rd;
  wire [3:0] opcode;
  wire [6:0] keyboard_1_data;
  wire [11:0] addr;
  wire [15:0] alu_2_data_out, ALUout, bit_extender_2_out, key_out, memory_latch_1_address_latched,
       memory_latch_1_data_in_latched, multiplexer_2_out, multiplexer_3_out, multiplexer_4_out,
       multiplexer_6_out, multiplexer_7_out, multiplexer_9_out, multiplexer_10_out, PC, PC_1, ram_1_dout,
       read_out, registerfile_1_rs2_contents, sx_immed;

  PCreg pcreg_1 (.data_in(multiplexer_7_out), .clk(clk), .write_enable(1'b1), .reset(reset), .data_out(PC));
  Clock clock_1 (.out(clk));
  TTY #(.rows(13), .cols(80), .trigger("falling")) tty_1 (.data(read_out[6:0]), .clk(clk), .we(tty_we), .clr(reset));
  ALU alu_1 (.A(16'h1), .B(PC), .shamt(3'b000), .data_out(PC_1));  // open: optype
  ROM #(.addrWidth(16), .dataWidth(16)) rom_1 (.addr(PC), .data({opcode, addr}));
  nor nor_1 (eq, ALUout[0], ALUout[1], ALUout[2], ALUout[3], ALUout[4], ALUout[5], ALUout[6], ALUout[7], ALUout[8], ALUout[9], ALUout[10], ALUout[11], ALUout[12], ALUout[13], ALUout[14], ALUout[15]);
  Multiplexer #(.width(3), .enable("false")) multiplexer_1 (
    .in0(rd), .in1(addr[8:6]), .out(multiplexer_1_out), .sel(Rdst));
  ALU alu_2 (.A(PC_1), .B(sx_immed), .shamt(3'b000), .data_out(alu_2_data_out));  // open: optype
  not not_1 (not_1_out, clk);
  Decoder #(.select(4)) decoder_1 (
    .out0(\output ), .out1(\input ), .out2(lw), .out3(sw), .out4(beq), .out5(bgt), .out6(\or ), .out7(\and ),
    .out8(addi), .out9(add), .out10(sub), .out11(shiftrt), .out12(shiftlft), .out13(j), .out14(jal),
    .out15(jr), .sel(opcode), .en(1'b1));
  or or_1 (jPCL, j, jal);
  not not_2 (not_2_out, ALUout[15]);
  not not_3 (not_3_out, eq);
  and and_1 (gt, not_2_out, not_3_out);
  and and_2 (and_2_out, eq, beq);
  and and_3 (and_3_out, gt, bgt);
  RegisterFile registerfile_1 (
    .rd(multiplexer_1_out), .data_in(multiplexer_3_out), .clk(not_1_out), .reset(reset), .write_enable(Rwe),
    .rs1(addr[11:9]), .rs2(addr[8:6]), .rs1_contents(read_out), .rs2_contents(registerfile_1_rs2_contents));
  assign sx_immed = {{10{addr[5]}}, addr[5:0]};  // Bit_Extender bit_extender_1
  or or_2 (or_2_out, and_2_out, and_3_out);
  Multiplexer #(.width(16), .enable("false")) multiplexer_2 (
    .in0(PC_1), .in1(alu_2_data_out), .out(multiplexer_2_out), .sel(or_2_out));
  Multiplexer #(.width(16), .enable("false")) multiplexer_3 (
    .in0(multiplexer_10_out), .in1(PC_1), .out(multiplexer_3_out), .sel(jal));
  Multiplexer #(.width(16), .enable("false")) multiplexer_4 (
    .in0(registerfile_1_rs2_contents), .in1(sx_immed), .out(multiplexer_4_out), .sel(ALUinB));
  Multiplexer #(.width(3), .enable("false")) multiplexer_5 (.in0(addr[5:3]), .in1(3'b111), .out(rd), .sel(jal));
  ALU alu_3 (.A(read_out), .B(multiplexer_4_out), .shamt(addr[2:0]), .optype(ALUop), .data_out(ALUout));
  Keyboard #(.trigger("falling")) keyboard_1 (
    .clk(clk), .re(key_re), .clr(reset), .avail(keyboard_1_avail), .data(keyboard_1_data));
  Multiplexer #(.width(16), .enable("false")) multiplexer_6 (
    .in0(multiplexer_2_out), .in1({PC[14], PC[15], PC[13:12], addr}), .out(multiplexer_6_out), .sel(jPCL));
  Multiplexer #(.width(16), .enable("false")) multiplexer_7 (
    .in0(multiplexer_6_out), .in1(read_out), .out(multiplexer_7_out), .sel(jr));
  or or_3 (DMwe, sw, 1'b0);
  or or_4 (ALUinB, sw, lw, addi);
  RAM #(.addrWidth(16), .dataWidth(16), .trigger("high"), .databus("bibus")) ram_1 (
    .addr(memory_latch_1_address_latched), .we(memory_latch_1_we_latched), .oe(memory_latch_1_oe_latched),
    .din(memory_latch_1_data_in_latched), .dout(ram_1_dout));
  memory_latch memory_latch_1 (
    .address(ALUout), .WE(DMwe), .clk(clk), .data_in(registerfile_1_rs2_contents),
    .address_latched(memory_latch_1_address_latched), .WE_latched(memory_latch_1_we_latched),
    .OE_latched(memory_latch_1_oe_latched), .data_in_latched(memory_latch_1_data_in_latched));
  assign bit_extender_2_out = {{9{1'b0}}, keyboard_1_data};  // Bit_Extender bit_extender_2
  or or_5 (Rwd, 1'b0, lw);
  or or_6 (Rwe, shiftlft, shiftrt, \input , lw, \output , addi, add, sub, \or , \and , shiftrt, jal);
  or or_7 (Rdst, lw, addi);
  or or_8 (key_re, 1'b0, \input );
  or or_9 (tty_we, 1'b0, \output );
  or or_10 (ALUop[0], sub, beq, shiftrt, \or , bgt);
  or or_11 (ALUop[1], \or , \and );
  or or_12 (ALUop[2], shiftrt, shiftlft);
  Multiplexer #(.width(16), .enable("false")) multiplexer_8 (
    .in0(bit_extender_2_out), .in1(16'h80), .out(key_out), .sel(not_4_out));
  not not_4 (not_4_out, keyboard_1_avail);
  Multiplexer #(.width(16), .enable("false")) multiplexer_9 (
    .in0(ALUout), .in1(ram_1_dout), .out(multiplexer_9_out), .sel(Rwd));
  Multiplexer #(.width(16), .enable("false")) multiplexer_10 (
    .in0(multiplexer_9_out), .in1(key_out), .out(multiplexer_10_out), .sel(key_re));

  // Other names for the same wires on the sheet: immed[5:0] = addr[5:0];
  //   PCL[15:0] = {PC[14], PC[15], PC[13:12], addr}; rs[2:0] = addr[11:9]; rt[2:0] = addr[8:6];
  //   shamt[2:0] = addr[2:0]; write_key = key_re

  // Notes on the sheet:
  //   PC + 1
  //   contents of rom_1 (hex, n*v repeats v):
  //   8100 8903 1008 82a0 400 893f 583b 403f
endmodule

module \reg  (
  input  [15:0] data_in,
  input  clk,
  input  write_enable,
  input  reset,
  output [15:0] data_out
);

  wire and_1_out;

  and and_1 (and_1_out, clk, write_enable);
  D_Flip_Flop d_ff_1 (.D(data_in[0]), .clk(and_1_out), .Q(data_out[0]), .reset(reset));  // open: Qn, preset
  D_Flip_Flop d_ff_2 (.D(data_in[1]), .clk(and_1_out), .Q(data_out[1]), .reset(reset));  // open: Qn, preset
  D_Flip_Flop d_ff_3 (.D(data_in[2]), .clk(and_1_out), .Q(data_out[2]), .reset(reset));  // open: Qn, preset
  D_Flip_Flop d_ff_4 (.D(data_in[3]), .clk(and_1_out), .Q(data_out[3]), .reset(reset));  // open: Qn, preset
  D_Flip_Flop d_ff_5 (.D(data_in[4]), .clk(and_1_out), .Q(data_out[4]), .reset(reset));  // open: Qn, preset
  D_Flip_Flop d_ff_6 (.D(data_in[5]), .clk(and_1_out), .Q(data_out[5]), .reset(reset));  // open: Qn, preset
  D_Flip_Flop d_ff_7 (.D(data_in[6]), .clk(and_1_out), .Q(data_out[6]), .reset(reset));  // open: Qn, preset
  D_Flip_Flop d_ff_8 (.D(data_in[7]), .clk(and_1_out), .Q(data_out[7]), .reset(reset));  // open: Qn, preset
  D_Flip_Flop d_ff_9 (.D(data_in[8]), .clk(and_1_out), .Q(data_out[8]), .reset(reset));  // open: Qn, preset
  D_Flip_Flop d_ff_10 (.D(data_in[9]), .clk(and_1_out), .Q(data_out[9]), .reset(reset));  // open: Qn, preset
  D_Flip_Flop d_ff_11 (.D(data_in[10]), .clk(and_1_out), .Q(data_out[10]), .reset(reset));  // open: Qn, preset
  D_Flip_Flop d_ff_12 (.D(data_in[11]), .clk(and_1_out), .Q(data_out[11]), .reset(reset));  // open: Qn, preset
  D_Flip_Flop d_ff_13 (.D(data_in[12]), .clk(and_1_out), .Q(data_out[12]), .reset(reset));  // open: Qn, preset
  D_Flip_Flop d_ff_14 (.D(data_in[13]), .clk(and_1_out), .Q(data_out[13]), .reset(reset));  // open: Qn, preset
  D_Flip_Flop d_ff_15 (.D(data_in[14]), .clk(and_1_out), .Q(data_out[14]), .reset(reset));  // open: Qn, preset
  D_Flip_Flop d_ff_16 (.D(data_in[15]), .clk(and_1_out), .Q(data_out[15]), .reset(reset));  // open: Qn, preset
endmodule

module RegisterFile (
  input  [2:0] rd,
  input  [15:0] data_in,
  input  clk,
  input  reset,
  input  write_enable,
  input  [2:0] rs1,
  input  [2:0] rs2,
  output [15:0] rs1_contents,
  output [15:0] rs2_contents
);

  wire decoder_1_out1, decoder_1_out2, decoder_1_out3, decoder_1_out4, decoder_1_out5, decoder_1_out6,
       decoder_1_out7;
  wire [15:0] reg_1_data_out, reg_2_data_out, reg_3_data_out, reg_4_data_out, reg_5_data_out, reg_6_data_out,
       reg_7_data_out;

  Decoder #(.select(3)) decoder_1 (
    .out1(decoder_1_out1), .out2(decoder_1_out2), .out3(decoder_1_out3), .out4(decoder_1_out4),
    .out5(decoder_1_out5), .out6(decoder_1_out6), .out7(decoder_1_out7), .sel(rd), .en(write_enable));  // open: out0
  \reg  reg_1 (.data_in(data_in), .clk(clk), .write_enable(decoder_1_out1), .reset(reset), .data_out(reg_1_data_out));
  \reg  reg_2 (.data_in(data_in), .clk(clk), .write_enable(decoder_1_out2), .reset(reset), .data_out(reg_2_data_out));
  \reg  reg_3 (.data_in(data_in), .clk(clk), .write_enable(decoder_1_out3), .reset(reset), .data_out(reg_3_data_out));
  \reg  reg_4 (.data_in(data_in), .clk(clk), .write_enable(decoder_1_out4), .reset(reset), .data_out(reg_4_data_out));
  \reg  reg_5 (.data_in(data_in), .clk(clk), .write_enable(decoder_1_out5), .reset(reset), .data_out(reg_5_data_out));
  \reg  reg_6 (.data_in(data_in), .clk(clk), .write_enable(decoder_1_out6), .reset(reset), .data_out(reg_6_data_out));
  \reg  reg_7 (.data_in(data_in), .clk(clk), .write_enable(decoder_1_out7), .reset(reset), .data_out(reg_7_data_out));
  // Probe on {16{1'b0}}
  Multiplexer #(.select(3), .width(16), .enable("false")) multiplexer_1 (
    .in0({16{1'b0}}), .in1(reg_1_data_out), .in2(reg_2_data_out), .in3(reg_3_data_out), .in4(reg_4_data_out),
    .in5(reg_5_data_out), .in6(reg_6_data_out), .in7(reg_7_data_out), .out(rs1_contents), .sel(rs1));
  Multiplexer #(.select(3), .width(16), .enable("false")) multiplexer_2 (
    .in0({16{1'b0}}), .in1(reg_1_data_out), .in2(reg_2_data_out), .in3(reg_3_data_out), .in4(reg_4_data_out),
    .in5(reg_5_data_out), .in6(reg_6_data_out), .in7(reg_7_data_out), .out(rs2_contents), .sel(rs2));
  // Probe on reg_1_data_out
  // Probe on reg_2_data_out
  // Probe on reg_3_data_out
  // Probe on reg_4_data_out
  // Probe on reg_5_data_out
  // Probe on reg_6_data_out
  // Probe on reg_7_data_out
endmodule

module ALU (
  input  [15:0] A,
  input  [15:0] B,
  input  [2:0] shamt,
  input  [2:0] optype,
  output [15:0] data_out
);

  wire [15:0] adder16_1_result, adder16_2_result, and_1_out, left_shifter_1_out, or_1_out,
       right_shifter_1_out;

  adder16 adder16_1 (.sub(1'b0), .result(adder16_1_result), .A(A), .B(B));  // open: ovf
  adder16 adder16_2 (.sub(1'b1), .result(adder16_2_result), .A(A), .B(B));  // open: ovf
  assign and_1_out = A & B;  // AND_Gate and_1, 16 bits wide
  assign or_1_out = B | A;  // OR_Gate or_1, 16 bits wide
  left_shifter left_shifter_1 (.shamt(shamt), .in(A), .out(left_shifter_1_out));
  right_shifter right_shifter_1 (.shamt(shamt), .in(A), .out(right_shifter_1_out));
  Multiplexer #(.select(3), .width(16), .enable("false")) multiplexer_1 (
    .in0(adder16_1_result), .in1(adder16_2_result), .in2(and_1_out), .in3(or_1_out),
    .in4(left_shifter_1_out), .in5(right_shifter_1_out), .out(data_out), .sel(optype));  // open: in6, in7
endmodule

module L_3aa3e677 (
  input  Cin,
  input  A,
  input  B,
  output Sum,
  output Cout
);

  wire and_1_out, and_2_out, xor_1_out;

  and and_1 (and_1_out, B, A);
  xor xor_1 (xor_1_out, A, B);
  and and_2 (and_2_out, xor_1_out, Cin);
  xor xor_2 (Sum, Cin, xor_1_out);
  or or_1 (Cout, and_2_out, and_1_out);
endmodule

module adder16 (
  input  sub,
  input  [15:0] A,
  input  [15:0] B,
  output [15:0] result,
  output ovf
);

  wire l_3aa3e677_1_cout, l_3aa3e677_2_cout, l_3aa3e677_3_cout, l_3aa3e677_4_cout, l_3aa3e677_5_cout,
       l_3aa3e677_6_cout, l_3aa3e677_7_cout, l_3aa3e677_8_cout, l_3aa3e677_9_cout, l_3aa3e677_10_cout,
       l_3aa3e677_11_cout, l_3aa3e677_12_cout, l_3aa3e677_13_cout, l_3aa3e677_14_cout, l_3aa3e677_15_cout,
       l_3aa3e677_16_cout, xor_2_out, xor_3_out, xor_4_out, xor_5_out, xor_6_out, xor_7_out, xor_8_out,
       xor_9_out, xor_10_out, xor_11_out, xor_12_out, xor_13_out, xor_14_out, xor_15_out, xor_16_out,
       xor_17_out;

  xor xor_1 (ovf, l_3aa3e677_2_cout, l_3aa3e677_1_cout);
  L_3aa3e677 l_3aa3e677_1 (
    .Cout(l_3aa3e677_1_cout), .Sum(result[15]), .B(xor_2_out), .A(A[15]), .Cin(l_3aa3e677_2_cout));
  xor xor_2 (xor_2_out, sub, B[15]);
  L_3aa3e677 l_3aa3e677_2 (
    .Cout(l_3aa3e677_2_cout), .Sum(result[14]), .B(xor_4_out), .A(A[14]), .Cin(l_3aa3e677_3_cout));
  xor xor_3 (xor_3_out, sub, B[13]);
  xor xor_4 (xor_4_out, sub, B[14]);
  L_3aa3e677 l_3aa3e677_3 (
    .Cout(l_3aa3e677_3_cout), .Sum(result[13]), .B(xor_3_out), .A(A[13]), .Cin(l_3aa3e677_4_cout));
  L_3aa3e677 l_3aa3e677_4 (
    .Cout(l_3aa3e677_4_cout), .Sum(result[12]), .B(xor_5_out), .A(A[12]), .Cin(l_3aa3e677_5_cout));
  xor xor_5 (xor_5_out, sub, B[12]);
  xor xor_6 (xor_6_out, sub, B[11]);
  L_3aa3e677 l_3aa3e677_5 (
    .Cout(l_3aa3e677_5_cout), .Sum(result[11]), .B(xor_6_out), .A(A[11]), .Cin(l_3aa3e677_6_cout));
  L_3aa3e677 l_3aa3e677_6 (
    .Cout(l_3aa3e677_6_cout), .Sum(result[10]), .B(xor_8_out), .A(A[10]), .Cin(l_3aa3e677_8_cout));
  xor xor_7 (xor_7_out, sub, B[9]);
  xor xor_8 (xor_8_out, sub, B[10]);
  L_3aa3e677 l_3aa3e677_7 (
    .Cout(l_3aa3e677_7_cout), .Sum(result[8]), .B(xor_10_out), .A(A[8]), .Cin(l_3aa3e677_9_cout));
  L_3aa3e677 l_3aa3e677_8 (.Cout(l_3aa3e677_8_cout), .Sum(result[9]), .B(xor_7_out), .A(A[9]), .Cin(l_3aa3e677_7_cout));
  xor xor_9 (xor_9_out, sub, B[7]);
  xor xor_10 (xor_10_out, sub, B[8]);
  L_3aa3e677 l_3aa3e677_9 (
    .Cout(l_3aa3e677_9_cout), .Sum(result[7]), .B(xor_9_out), .A(A[7]), .Cin(l_3aa3e677_10_cout));
  L_3aa3e677 l_3aa3e677_10 (
    .Cout(l_3aa3e677_10_cout), .Sum(result[6]), .B(xor_12_out), .A(A[6]), .Cin(l_3aa3e677_12_cout));
  xor xor_11 (xor_11_out, sub, B[5]);
  xor xor_12 (xor_12_out, sub, B[6]);
  L_3aa3e677 l_3aa3e677_11 (
    .Cout(l_3aa3e677_11_cout), .Sum(result[4]), .B(xor_14_out), .A(A[4]), .Cin(l_3aa3e677_14_cout));
  L_3aa3e677 l_3aa3e677_12 (
    .Cout(l_3aa3e677_12_cout), .Sum(result[5]), .B(xor_11_out), .A(A[5]), .Cin(l_3aa3e677_11_cout));
  xor xor_13 (xor_13_out, sub, B[3]);
  xor xor_14 (xor_14_out, sub, B[4]);
  L_3aa3e677 l_3aa3e677_13 (
    .Cout(l_3aa3e677_13_cout), .Sum(result[2]), .B(xor_16_out), .A(A[2]), .Cin(l_3aa3e677_15_cout));
  L_3aa3e677 l_3aa3e677_14 (
    .Cout(l_3aa3e677_14_cout), .Sum(result[3]), .B(xor_13_out), .A(A[3]), .Cin(l_3aa3e677_13_cout));
  xor xor_15 (xor_15_out, sub, B[1]);
  xor xor_16 (xor_16_out, sub, B[2]);
  L_3aa3e677 l_3aa3e677_15 (
    .Cout(l_3aa3e677_15_cout), .Sum(result[1]), .B(xor_15_out), .A(A[1]), .Cin(l_3aa3e677_16_cout));
  L_3aa3e677 l_3aa3e677_16 (.Cout(l_3aa3e677_16_cout), .Sum(result[0]), .B(xor_17_out), .A(A[0]), .Cin(sub));
  xor xor_17 (xor_17_out, sub, B[0]);
endmodule

module left_shifter (
  input  [15:0] in,
  input  [2:0] shamt,
  output [15:0] out
);

  wire multiplexer_1_out, multiplexer_2_out, multiplexer_3_out, multiplexer_4_out, multiplexer_5_out,
       multiplexer_6_out, multiplexer_7_out, multiplexer_8_out, multiplexer_9_out, multiplexer_10_out,
       multiplexer_11_out, multiplexer_12_out, multiplexer_13_out, multiplexer_14_out, multiplexer_15_out,
       multiplexer_16_out, multiplexer_17_out, multiplexer_18_out, multiplexer_19_out, multiplexer_20_out,
       multiplexer_21_out, multiplexer_22_out, multiplexer_23_out, multiplexer_24_out, multiplexer_25_out,
       multiplexer_26_out, multiplexer_27_out, multiplexer_28_out, multiplexer_30_out, multiplexer_31_out,
       multiplexer_34_out, multiplexer_35_out;

  Multiplexer #(.enable("false")) multiplexer_1 (.in0(in[15]), .in1(in[14]), .out(multiplexer_1_out), .sel(shamt[0]));
  Multiplexer #(.enable("false")) multiplexer_2 (.in0(in[14]), .in1(in[13]), .out(multiplexer_2_out), .sel(shamt[0]));
  Multiplexer #(.enable("false")) multiplexer_3 (.in0(in[13]), .in1(in[12]), .out(multiplexer_3_out), .sel(shamt[0]));
  Multiplexer #(.enable("false")) multiplexer_4 (.in0(in[12]), .in1(in[11]), .out(multiplexer_4_out), .sel(shamt[0]));
  Multiplexer #(.enable("false")) multiplexer_5 (.in0(in[11]), .in1(in[10]), .out(multiplexer_5_out), .sel(shamt[0]));
  Multiplexer #(.enable("false")) multiplexer_6 (.in0(in[10]), .in1(in[9]), .out(multiplexer_6_out), .sel(shamt[0]));
  Multiplexer #(.enable("false")) multiplexer_7 (.in0(in[9]), .in1(in[8]), .out(multiplexer_7_out), .sel(shamt[0]));
  Multiplexer #(.enable("false")) multiplexer_8 (.in0(in[8]), .in1(in[7]), .out(multiplexer_8_out), .sel(shamt[0]));
  Multiplexer #(.enable("false")) multiplexer_9 (.in0(in[7]), .in1(in[6]), .out(multiplexer_9_out), .sel(shamt[0]));
  Multiplexer #(.enable("false")) multiplexer_10 (.in0(in[6]), .in1(in[5]), .out(multiplexer_10_out), .sel(shamt[0]));
  Multiplexer #(.enable("false")) multiplexer_11 (.in0(in[5]), .in1(in[4]), .out(multiplexer_11_out), .sel(shamt[0]));
  Multiplexer #(.enable("false")) multiplexer_12 (.in0(in[4]), .in1(in[3]), .out(multiplexer_12_out), .sel(shamt[0]));
  Multiplexer #(.enable("false")) multiplexer_13 (.in0(in[3]), .in1(in[2]), .out(multiplexer_13_out), .sel(shamt[0]));
  Multiplexer #(.enable("false")) multiplexer_14 (.in0(in[2]), .in1(in[1]), .out(multiplexer_14_out), .sel(shamt[0]));
  Multiplexer #(.enable("false")) multiplexer_15 (.in0(in[1]), .in1(in[0]), .out(multiplexer_15_out), .sel(shamt[0]));
  Multiplexer #(.enable("false")) multiplexer_16 (.in0(in[0]), .in1(1'b0), .out(multiplexer_16_out), .sel(shamt[0]));
  Multiplexer #(.enable("false")) multiplexer_17 (
    .in0(multiplexer_1_out), .in1(multiplexer_3_out), .out(multiplexer_17_out), .sel(shamt[1]));
  Multiplexer #(.enable("false")) multiplexer_18 (
    .in0(multiplexer_2_out), .in1(multiplexer_4_out), .out(multiplexer_18_out), .sel(shamt[1]));
  Multiplexer #(.enable("false")) multiplexer_19 (
    .in0(multiplexer_3_out), .in1(multiplexer_5_out), .out(multiplexer_19_out), .sel(shamt[1]));
  Multiplexer #(.enable("false")) multiplexer_20 (
    .in0(multiplexer_4_out), .in1(multiplexer_6_out), .out(multiplexer_20_out), .sel(shamt[1]));
  Multiplexer #(.enable("false")) multiplexer_21 (
    .in0(multiplexer_5_out), .in1(multiplexer_7_out), .out(multiplexer_21_out), .sel(shamt[1]));
  Multiplexer #(.enable("false")) multiplexer_22 (
    .in0(multiplexer_6_out), .in1(multiplexer_8_out), .out(multiplexer_22_out), .sel(shamt[1]));
  Multiplexer #(.enable("false")) multiplexer_23 (
    .in0(multiplexer_7_out), .in1(multiplexer_9_out), .out(multiplexer_23_out), .sel(shamt[1]));
  Multiplexer #(.enable("false")) multiplexer_24 (
    .in0(multiplexer_8_out), .in1(multiplexer_10_out), .out(multiplexer_24_out), .sel(shamt[1]));
  Multiplexer #(.enable("false")) multiplexer_25 (
    .in0(multiplexer_9_out), .in1(multiplexer_11_out), .out(multiplexer_25_out), .sel(shamt[1]));
  Multiplexer #(.enable("false")) multiplexer_26 (
    .in0(multiplexer_10_out), .in1(multiplexer_12_out), .out(multiplexer_26_out), .sel(shamt[1]));
  Multiplexer #(.enable("false")) multiplexer_27 (
    .in0(multiplexer_11_out), .in1(multiplexer_13_out), .out(multiplexer_27_out), .sel(shamt[1]));
  Multiplexer #(.enable("false")) multiplexer_28 (
    .in0(multiplexer_12_out), .in1(multiplexer_14_out), .out(multiplexer_28_out), .sel(shamt[1]));
  Multiplexer #(.enable("false")) multiplexer_29 (
    .in0(multiplexer_17_out), .in1(multiplexer_21_out), .out(out[15]), .sel(shamt[2]));
  Multiplexer #(.enable("false")) multiplexer_30 (
    .in0(multiplexer_13_out), .in1(multiplexer_15_out), .out(multiplexer_30_out), .sel(shamt[1]));
  Multiplexer #(.enable("false")) multiplexer_31 (
    .in0(multiplexer_14_out), .in1(multiplexer_16_out), .out(multiplexer_31_out), .sel(shamt[1]));
  Multiplexer #(.enable("false")) multiplexer_32 (
    .in0(multiplexer_18_out), .in1(multiplexer_22_out), .out(out[14]), .sel(shamt[2]));
  Multiplexer #(.enable("false")) multiplexer_33 (
    .in0(multiplexer_19_out), .in1(multiplexer_23_out), .out(out[13]), .sel(shamt[2]));
  Multiplexer #(.enable("false")) multiplexer_34 (
    .in0(multiplexer_15_out), .in1(1'b0), .out(multiplexer_34_out), .sel(shamt[1]));
  Multiplexer #(.enable("false")) multiplexer_35 (
    .in0(multiplexer_16_out), .in1(1'b0), .out(multiplexer_35_out), .sel(shamt[1]));
  Multiplexer #(.enable("false")) multiplexer_36 (
    .in0(multiplexer_20_out), .in1(multiplexer_24_out), .out(out[12]), .sel(shamt[2]));
  Multiplexer #(.enable("false")) multiplexer_37 (
    .in0(multiplexer_21_out), .in1(multiplexer_25_out), .out(out[11]), .sel(shamt[2]));
  Multiplexer #(.enable("false")) multiplexer_38 (
    .in0(multiplexer_22_out), .in1(multiplexer_26_out), .out(out[10]), .sel(shamt[2]));
  Multiplexer #(.enable("false")) multiplexer_39 (
    .in0(multiplexer_23_out), .in1(multiplexer_27_out), .out(out[9]), .sel(shamt[2]));
  Multiplexer #(.enable("false")) multiplexer_40 (
    .in0(multiplexer_24_out), .in1(multiplexer_28_out), .out(out[8]), .sel(shamt[2]));
  Multiplexer #(.enable("false")) multiplexer_41 (
    .in0(multiplexer_25_out), .in1(multiplexer_30_out), .out(out[7]), .sel(shamt[2]));
  Multiplexer #(.enable("false")) multiplexer_42 (
    .in0(multiplexer_26_out), .in1(multiplexer_31_out), .out(out[6]), .sel(shamt[2]));
  Multiplexer #(.enable("false")) multiplexer_43 (
    .in0(multiplexer_27_out), .in1(multiplexer_34_out), .out(out[5]), .sel(shamt[2]));
  Multiplexer #(.enable("false")) multiplexer_44 (
    .in0(multiplexer_28_out), .in1(multiplexer_35_out), .out(out[4]), .sel(shamt[2]));
  Multiplexer #(.enable("false")) multiplexer_45 (.in0(multiplexer_30_out), .in1(1'b0), .out(out[3]), .sel(shamt[2]));
  Multiplexer #(.enable("false")) multiplexer_46 (.in0(multiplexer_31_out), .in1(1'b0), .out(out[2]), .sel(shamt[2]));
  Multiplexer #(.enable("false")) multiplexer_47 (.in0(multiplexer_34_out), .in1(1'b0), .out(out[1]), .sel(shamt[2]));
  Multiplexer #(.enable("false")) multiplexer_48 (.in0(multiplexer_35_out), .in1(1'b0), .out(out[0]), .sel(shamt[2]));

  // Other names for the same wires on the sheet: shift = shamt[0]; sh1 = shamt[1]; sh2 = shamt[2]
endmodule

module tet (
  input  [2:0] rd,
  input  reset,
  input  reg_write_enable,
  input  [2:0] rs1,
  input  [2:0] rs2
);

  wire clk_out;
  wire [3:0] opcode;
  wire [11:0] addr;
  wire [15:0] alu_1_p4, alu_2_data_out, alu_3_data_out, multiplexer_1_out, multiplexer_2_out,
       multiplexer_3_out, PC_data_out, ram_1_data, registerfile_1_rs1_contents, registerfile_1_rs2_contents;

  \reg  PC (.data_in(multiplexer_2_out), .clk(clk_out), .write_enable(1'b1), .reset(reset), .data_out(PC_data_out));
  Keyboard keyboard_1 (.clk(clk_out));  // open: re, clr, avail, data
  // ALU alu_1: pin names not known; wires that end beside it: PC_data_out, PC_data_out, 2'b00, alu_1_p4
  Clock clk (.out(clk_out));
  TTY #(.rows(13), .cols(80), .trigger("falling")) tty_1 ();  // open: data, clk, we, clr
  ROM #(.addrWidth(16), .dataWidth(16)) rom_1 (.addr(PC_data_out), .data({addr, opcode}));
  ALU alu_2 (.A(alu_1_p4), .data_out(alu_2_data_out));  // open: B, shamt, optype
  Multiplexer #(.width(16), .enable("false")) multiplexer_1 (
    .in0(alu_1_p4), .in1(alu_2_data_out), .out(multiplexer_1_out));  // open: sel
  RegisterFile registerfile_1 (
    .rd(rd), .data_in(multiplexer_3_out), .clk(clk_out), .reset(reset), .write_enable(reg_write_enable),
    .rs1(rs1), .rs2(rs2), .rs1_contents(registerfile_1_rs1_contents),
    .rs2_contents(registerfile_1_rs2_contents));
  Multiplexer #(.width(16), .enable("false")) multiplexer_2 (
    .in0(multiplexer_1_out), .out(multiplexer_2_out));  // open: in1, sel
  ALU alu_3 (
    .A(registerfile_1_rs1_contents), .B(registerfile_1_rs2_contents), .data_out(alu_3_data_out));  // open: shamt, optype
  RAM #(.addrWidth(16), .dataWidth(16)) ram_1 (.addr(alu_3_data_out), .data(ram_1_data));  // open: we, oe, clk
  Multiplexer #(.width(16), .enable("false")) multiplexer_3 (
    .in0(alu_3_data_out), .in1(ram_1_data), .out(multiplexer_3_out));  // open: sel
  // also tied to GND on the sheet: {PC_data_out[1], PC_data_out[2], PC_data_out[3], PC_data_out[4], PC_data_out[5], PC_data_out[6], PC_data_out[7], PC_data_out[8], PC_data_out[9], PC_data_out[10], PC_data_out[11], PC_data_out[12], PC_data_out[13], PC_data_out[14], PC_data_out[15]}
  // also tied to VCC on the sheet: PC_data_out[0]

  // Other names for the same wires on the sheet: rs[2:0] = addr[2:0]; rt[2:0] = addr[5:3]; imm[5:0] = addr[11:6];
  //   rd_t[2:0] = addr[8:6]
endmodule

module left1 (
  input  [15:0] in,
  input  [2:0] shamt,
  output [15:0] out
);

  wire multiplexer_1_out, multiplexer_2_out, multiplexer_3_out, multiplexer_4_out, multiplexer_5_out,
       multiplexer_6_out, multiplexer_7_out, multiplexer_8_out, multiplexer_9_out, multiplexer_10_out,
       multiplexer_11_out, multiplexer_12_out, multiplexer_13_out, multiplexer_14_out, multiplexer_15_out,
       multiplexer_16_out, multiplexer_17_out, multiplexer_18_out, multiplexer_19_out, multiplexer_20_out,
       multiplexer_21_out, multiplexer_22_out, multiplexer_23_out, multiplexer_24_out, multiplexer_25_out,
       multiplexer_26_out, multiplexer_27_out, multiplexer_28_out, multiplexer_30_out, multiplexer_31_out,
       multiplexer_34_out, multiplexer_35_out;

  Multiplexer #(.enable("false")) multiplexer_1 (.in0(in[15]), .in1(in[14]), .out(multiplexer_1_out), .sel(shamt[0]));
  Multiplexer #(.enable("false")) multiplexer_2 (.in0(in[14]), .in1(in[13]), .out(multiplexer_2_out), .sel(shamt[0]));
  Multiplexer #(.enable("false")) multiplexer_3 (.in0(in[13]), .in1(in[12]), .out(multiplexer_3_out), .sel(shamt[0]));
  Multiplexer #(.enable("false")) multiplexer_4 (.in0(in[12]), .in1(in[11]), .out(multiplexer_4_out), .sel(shamt[0]));
  Multiplexer #(.enable("false")) multiplexer_5 (.in0(in[11]), .in1(in[10]), .out(multiplexer_5_out), .sel(shamt[0]));
  Multiplexer #(.enable("false")) multiplexer_6 (.in0(in[10]), .in1(in[9]), .out(multiplexer_6_out), .sel(shamt[0]));
  Multiplexer #(.enable("false")) multiplexer_7 (.in0(in[9]), .in1(in[8]), .out(multiplexer_7_out), .sel(shamt[0]));
  Multiplexer #(.enable("false")) multiplexer_8 (.in0(in[8]), .in1(in[7]), .out(multiplexer_8_out), .sel(shamt[0]));
  Multiplexer #(.enable("false")) multiplexer_9 (.in0(in[7]), .in1(in[6]), .out(multiplexer_9_out), .sel(shamt[0]));
  Multiplexer #(.enable("false")) multiplexer_10 (.in0(in[6]), .in1(in[5]), .out(multiplexer_10_out), .sel(shamt[0]));
  Multiplexer #(.enable("false")) multiplexer_11 (.in0(in[5]), .in1(in[4]), .out(multiplexer_11_out), .sel(shamt[0]));
  Multiplexer #(.enable("false")) multiplexer_12 (.in0(in[4]), .in1(in[3]), .out(multiplexer_12_out), .sel(shamt[0]));
  Multiplexer #(.enable("false")) multiplexer_13 (.in0(in[3]), .in1(in[2]), .out(multiplexer_13_out), .sel(shamt[0]));
  Multiplexer #(.enable("false")) multiplexer_14 (.in0(in[2]), .in1(in[1]), .out(multiplexer_14_out), .sel(shamt[0]));
  Multiplexer #(.enable("false")) multiplexer_15 (.in0(in[1]), .in1(in[0]), .out(multiplexer_15_out), .sel(shamt[0]));
  Multiplexer #(.enable("false")) multiplexer_16 (.in0(in[0]), .in1(1'b0), .out(multiplexer_16_out), .sel(shamt[0]));
  Multiplexer #(.enable("false")) multiplexer_17 (
    .in0(multiplexer_1_out), .in1(multiplexer_3_out), .out(multiplexer_17_out), .sel(shamt[1]));
  Multiplexer #(.enable("false")) multiplexer_18 (
    .in0(multiplexer_2_out), .in1(multiplexer_4_out), .out(multiplexer_18_out), .sel(shamt[1]));
  Multiplexer #(.enable("false")) multiplexer_19 (
    .in0(multiplexer_3_out), .in1(multiplexer_5_out), .out(multiplexer_19_out), .sel(shamt[1]));
  Multiplexer #(.enable("false")) multiplexer_20 (
    .in0(multiplexer_4_out), .in1(multiplexer_6_out), .out(multiplexer_20_out), .sel(shamt[1]));
  Multiplexer #(.enable("false")) multiplexer_21 (
    .in0(multiplexer_5_out), .in1(multiplexer_7_out), .out(multiplexer_21_out), .sel(shamt[1]));
  Multiplexer #(.enable("false")) multiplexer_22 (
    .in0(multiplexer_6_out), .in1(multiplexer_8_out), .out(multiplexer_22_out), .sel(shamt[1]));
  Multiplexer #(.enable("false")) multiplexer_23 (
    .in0(multiplexer_7_out), .in1(multiplexer_9_out), .out(multiplexer_23_out), .sel(shamt[1]));
  Multiplexer #(.enable("false")) multiplexer_24 (
    .in0(multiplexer_8_out), .in1(multiplexer_10_out), .out(multiplexer_24_out), .sel(shamt[1]));
  Multiplexer #(.enable("false")) multiplexer_25 (
    .in0(multiplexer_9_out), .in1(multiplexer_11_out), .out(multiplexer_25_out), .sel(shamt[1]));
  Multiplexer #(.enable("false")) multiplexer_26 (
    .in0(multiplexer_10_out), .in1(multiplexer_12_out), .out(multiplexer_26_out), .sel(shamt[1]));
  Multiplexer #(.enable("false")) multiplexer_27 (
    .in0(multiplexer_11_out), .in1(multiplexer_13_out), .out(multiplexer_27_out), .sel(shamt[1]));
  Multiplexer #(.enable("false")) multiplexer_28 (
    .in0(multiplexer_12_out), .in1(multiplexer_14_out), .out(multiplexer_28_out), .sel(shamt[1]));
  Multiplexer #(.enable("false")) multiplexer_29 (
    .in0(multiplexer_17_out), .in1(multiplexer_21_out), .out(out[15]), .sel(shamt[2]));
  Multiplexer #(.enable("false")) multiplexer_30 (
    .in0(multiplexer_13_out), .in1(multiplexer_15_out), .out(multiplexer_30_out), .sel(shamt[1]));
  Multiplexer #(.enable("false")) multiplexer_31 (
    .in0(multiplexer_14_out), .in1(multiplexer_16_out), .out(multiplexer_31_out), .sel(shamt[1]));
  Multiplexer #(.enable("false")) multiplexer_32 (
    .in0(multiplexer_18_out), .in1(multiplexer_22_out), .out(out[14]), .sel(shamt[2]));
  Multiplexer #(.enable("false")) multiplexer_33 (
    .in0(multiplexer_19_out), .in1(multiplexer_23_out), .out(out[13]), .sel(shamt[2]));
  Multiplexer #(.enable("false")) multiplexer_34 (
    .in0(multiplexer_15_out), .in1(1'b0), .out(multiplexer_34_out), .sel(shamt[1]));
  Multiplexer #(.enable("false")) multiplexer_35 (
    .in0(multiplexer_16_out), .in1(1'b0), .out(multiplexer_35_out), .sel(shamt[1]));
  Multiplexer #(.enable("false")) multiplexer_36 (
    .in0(multiplexer_20_out), .in1(multiplexer_24_out), .out(out[12]), .sel(shamt[2]));
  Multiplexer #(.enable("false")) multiplexer_37 (
    .in0(multiplexer_21_out), .in1(multiplexer_25_out), .out(out[11]), .sel(shamt[2]));
  Multiplexer #(.enable("false")) multiplexer_38 (
    .in0(multiplexer_22_out), .in1(multiplexer_26_out), .out(out[10]), .sel(shamt[2]));
  Multiplexer #(.enable("false")) multiplexer_39 (
    .in0(multiplexer_23_out), .in1(multiplexer_27_out), .out(out[9]), .sel(shamt[2]));
  Multiplexer #(.enable("false")) multiplexer_40 (
    .in0(multiplexer_24_out), .in1(multiplexer_28_out), .out(out[8]), .sel(shamt[2]));
  Multiplexer #(.enable("false")) multiplexer_41 (
    .in0(multiplexer_25_out), .in1(multiplexer_30_out), .out(out[7]), .sel(shamt[2]));
  Multiplexer #(.enable("false")) multiplexer_42 (
    .in0(multiplexer_26_out), .in1(multiplexer_31_out), .out(out[6]), .sel(shamt[2]));
  Multiplexer #(.enable("false")) multiplexer_43 (
    .in0(multiplexer_27_out), .in1(multiplexer_34_out), .out(out[5]), .sel(shamt[2]));
  Multiplexer #(.enable("false")) multiplexer_44 (
    .in0(multiplexer_28_out), .in1(multiplexer_35_out), .out(out[4]), .sel(shamt[2]));
  Multiplexer #(.enable("false")) multiplexer_45 (.in0(multiplexer_30_out), .in1(1'b0), .out(out[3]), .sel(shamt[2]));
  Multiplexer #(.enable("false")) multiplexer_46 (.in0(multiplexer_31_out), .in1(1'b0), .out(out[2]), .sel(shamt[2]));
  Multiplexer #(.enable("false")) multiplexer_47 (.in0(multiplexer_34_out), .in1(1'b0), .out(out[1]), .sel(shamt[2]));
  Multiplexer #(.enable("false")) multiplexer_48 (.in0(multiplexer_35_out), .in1(1'b0), .out(out[0]), .sel(shamt[2]));

  // Other names for the same wires on the sheet: shift = shamt[0]; sh1 = shamt[1]; sh2 = shamt[2]
endmodule

module right_shifter (
  input  [15:0] in,
  input  [2:0] shamt,
  output [15:0] out
);

  wire multiplexer_1_out, multiplexer_2_out, multiplexer_3_out, multiplexer_4_out, multiplexer_7_out,
       multiplexer_8_out, multiplexer_10_out, multiplexer_11_out, multiplexer_12_out, multiplexer_13_out,
       multiplexer_16_out, multiplexer_17_out, multiplexer_19_out, multiplexer_20_out, multiplexer_21_out,
       multiplexer_22_out, multiplexer_25_out, multiplexer_26_out, multiplexer_27_out, multiplexer_28_out,
       multiplexer_31_out, multiplexer_32_out, multiplexer_34_out, multiplexer_35_out, multiplexer_36_out,
       multiplexer_37_out, multiplexer_40_out, multiplexer_41_out, multiplexer_43_out, multiplexer_44_out,
       multiplexer_45_out, multiplexer_46_out, not_1_out, not_2_out, not_3_out;

  not not_1 (not_1_out, shamt[0]);
  not not_2 (not_2_out, shamt[1]);
  not not_3 (not_3_out, shamt[2]);
  Multiplexer #(.enable("false")) multiplexer_1 (.in0(in[15]), .in1(in[14]), .out(multiplexer_1_out), .sel(not_1_out));
  Multiplexer #(.enable("false")) multiplexer_2 (.in0(in[15]), .in1(in[15]), .out(multiplexer_2_out), .sel(not_1_out));
  Multiplexer #(.enable("false")) multiplexer_3 (
    .in0(multiplexer_1_out), .in1(multiplexer_1_out), .out(multiplexer_3_out), .sel(not_2_out));
  Multiplexer #(.enable("false")) multiplexer_4 (
    .in0(multiplexer_2_out), .in1(multiplexer_2_out), .out(multiplexer_4_out), .sel(not_2_out));
  Multiplexer #(.enable("false")) multiplexer_5 (
    .in0(multiplexer_4_out), .in1(multiplexer_4_out), .out(out[15]), .sel(not_3_out));
  Multiplexer #(.enable("false")) multiplexer_6 (
    .in0(multiplexer_3_out), .in1(multiplexer_3_out), .out(out[14]), .sel(not_3_out));
  Multiplexer #(.enable("false")) multiplexer_7 (.in0(in[14]), .in1(in[13]), .out(multiplexer_7_out), .sel(not_1_out));
  Multiplexer #(.enable("false")) multiplexer_8 (
    .in0(multiplexer_2_out), .in1(multiplexer_7_out), .out(multiplexer_8_out), .sel(not_2_out));
  Multiplexer #(.enable("false")) multiplexer_9 (
    .in0(multiplexer_8_out), .in1(multiplexer_8_out), .out(out[13]), .sel(not_3_out));
  Multiplexer #(.enable("false")) multiplexer_10 (
    .in0(in[12]), .in1(in[11]), .out(multiplexer_10_out), .sel(not_1_out));
  Multiplexer #(.enable("false")) multiplexer_11 (
    .in0(in[13]), .in1(in[12]), .out(multiplexer_11_out), .sel(not_1_out));
  Multiplexer #(.enable("false")) multiplexer_12 (
    .in0(multiplexer_1_out), .in1(multiplexer_11_out), .out(multiplexer_12_out), .sel(not_2_out));
  Multiplexer #(.enable("false")) multiplexer_13 (
    .in0(multiplexer_7_out), .in1(multiplexer_10_out), .out(multiplexer_13_out), .sel(not_2_out));
  Multiplexer #(.enable("false")) multiplexer_14 (
    .in0(multiplexer_4_out), .in1(multiplexer_13_out), .out(out[11]), .sel(not_3_out));
  Multiplexer #(.enable("false")) multiplexer_15 (
    .in0(multiplexer_12_out), .in1(multiplexer_12_out), .out(out[12]), .sel(not_3_out));
  Multiplexer #(.enable("false")) multiplexer_16 (
    .in0(in[11]), .in1(in[10]), .out(multiplexer_16_out), .sel(not_1_out));
  Multiplexer #(.enable("false")) multiplexer_17 (
    .in0(multiplexer_11_out), .in1(multiplexer_16_out), .out(multiplexer_17_out), .sel(not_2_out));
  Multiplexer #(.enable("false")) multiplexer_18 (
    .in0(multiplexer_3_out), .in1(multiplexer_17_out), .out(out[10]), .sel(not_3_out));
  Multiplexer #(.enable("false")) multiplexer_19 (.in0(in[10]), .in1(in[9]), .out(multiplexer_19_out), .sel(not_1_out));
  Multiplexer #(.enable("false")) multiplexer_20 (.in0(in[9]), .in1(in[8]), .out(multiplexer_20_out), .sel(not_1_out));
  Multiplexer #(.enable("false")) multiplexer_21 (
    .in0(multiplexer_10_out), .in1(multiplexer_19_out), .out(multiplexer_21_out), .sel(not_2_out));
  Multiplexer #(.enable("false")) multiplexer_22 (
    .in0(multiplexer_16_out), .in1(multiplexer_20_out), .out(multiplexer_22_out), .sel(not_2_out));
  Multiplexer #(.enable("false")) multiplexer_23 (
    .in0(multiplexer_12_out), .in1(multiplexer_22_out), .out(out[8]), .sel(not_3_out));
  Multiplexer #(.enable("false")) multiplexer_24 (
    .in0(multiplexer_8_out), .in1(multiplexer_21_out), .out(out[9]), .sel(not_3_out));
  Multiplexer #(.enable("false")) multiplexer_25 (.in0(in[8]), .in1(in[7]), .out(multiplexer_25_out), .sel(not_1_out));
  Multiplexer #(.enable("false")) multiplexer_26 (.in0(in[7]), .in1(in[6]), .out(multiplexer_26_out), .sel(not_1_out));
  Multiplexer #(.enable("false")) multiplexer_27 (
    .in0(multiplexer_20_out), .in1(multiplexer_26_out), .out(multiplexer_27_out), .sel(not_2_out));
  Multiplexer #(.enable("false")) multiplexer_28 (
    .in0(multiplexer_19_out), .in1(multiplexer_25_out), .out(multiplexer_28_out), .sel(not_2_out));
  Multiplexer #(.enable("false")) multiplexer_29 (
    .in0(multiplexer_17_out), .in1(multiplexer_27_out), .out(out[6]), .sel(not_3_out));
  Multiplexer #(.enable("false")) multiplexer_30 (
    .in0(multiplexer_13_out), .in1(multiplexer_28_out), .out(out[7]), .sel(not_3_out));
  Multiplexer #(.enable("false")) multiplexer_31 (.in0(in[6]), .in1(in[5]), .out(multiplexer_31_out), .sel(not_1_out));
  Multiplexer #(.enable("false")) multiplexer_32 (
    .in0(multiplexer_25_out), .in1(multiplexer_31_out), .out(multiplexer_32_out), .sel(not_2_out));
  Multiplexer #(.enable("false")) multiplexer_33 (
    .in0(multiplexer_21_out), .in1(multiplexer_32_out), .out(out[5]), .sel(not_3_out));
  Multiplexer #(.enable("false")) multiplexer_34 (.in0(in[4]), .in1(in[3]), .out(multiplexer_34_out), .sel(not_1_out));
  Multiplexer #(.enable("false")) multiplexer_35 (.in0(in[5]), .in1(in[4]), .out(multiplexer_35_out), .sel(not_1_out));
  Multiplexer #(.enable("false")) multiplexer_36 (
    .in0(multiplexer_31_out), .in1(multiplexer_34_out), .out(multiplexer_36_out), .sel(not_2_out));
  Multiplexer #(.enable("false")) multiplexer_37 (
    .in0(multiplexer_26_out), .in1(multiplexer_35_out), .out(multiplexer_37_out), .sel(not_2_out));
  Multiplexer #(.enable("false")) multiplexer_38 (
    .in0(multiplexer_28_out), .in1(multiplexer_36_out), .out(out[3]), .sel(not_3_out));
  Multiplexer #(.enable("false")) multiplexer_39 (
    .in0(multiplexer_22_out), .in1(multiplexer_37_out), .out(out[4]), .sel(not_3_out));
  Multiplexer #(.enable("false")) multiplexer_40 (.in0(in[3]), .in1(in[2]), .out(multiplexer_40_out), .sel(not_1_out));
  Multiplexer #(.enable("false")) multiplexer_41 (
    .in0(multiplexer_35_out), .in1(multiplexer_40_out), .out(multiplexer_41_out), .sel(not_2_out));
  Multiplexer #(.enable("false")) multiplexer_42 (
    .in0(multiplexer_27_out), .in1(multiplexer_41_out), .out(out[2]), .sel(not_3_out));
  Multiplexer #(.enable("false")) multiplexer_43 (.in0(in[2]), .in1(in[1]), .out(multiplexer_43_out), .sel(not_1_out));
  Multiplexer #(.enable("false")) multiplexer_44 (.in0(in[1]), .in1(in[0]), .out(multiplexer_44_out), .sel(not_1_out));
  Multiplexer #(.enable("false")) multiplexer_45 (
    .in0(multiplexer_34_out), .in1(multiplexer_43_out), .out(multiplexer_45_out), .sel(not_2_out));
  Multiplexer #(.enable("false")) multiplexer_46 (
    .in0(multiplexer_40_out), .in1(multiplexer_44_out), .out(multiplexer_46_out), .sel(not_2_out));
  Multiplexer #(.enable("false")) multiplexer_47 (
    .in0(multiplexer_37_out), .in1(multiplexer_46_out), .out(out[0]), .sel(not_3_out));
  Multiplexer #(.enable("false")) multiplexer_48 (
    .in0(multiplexer_32_out), .in1(multiplexer_45_out), .out(out[1]), .sel(not_3_out));

  // Other names for the same wires on the sheet: shift = shamt[0]; sh1 = shamt[1]; sh2 = shamt[2]
endmodule

module memory_latch (
  input  [15:0] address,
  input  WE,
  input  clk,
  input  [15:0] data_in,
  output [15:0] address_latched,
  output WE_latched,
  output OE_latched,
  output [15:0] data_in_latched
);

  wire d_ff_1_q;
  wire [15:0] register_1_q;

  Register #(.width(16), .trigger("falling")) register_1 (
    .D(address), .en(WE), .clk(clk), .Q(register_1_q));  // open: clr
  D_Flip_Flop #(.trigger("falling")) d_ff_1 (.D(WE), .clk(clk), .Q(d_ff_1_q));  // open: Qn, preset, reset
  Register #(.width(16), .trigger("falling")) register_2 (
    .D(data_in), .en(WE), .clk(clk), .Q(data_in_latched));  // open: clr
  Multiplexer #(.width(16), .enable("false")) multiplexer_1 (
    .in0(address), .in1(register_1_q), .out(address_latched), .sel(d_ff_1_q));
  and and_1 (WE_latched, clk, d_ff_1_q);
  not not_1 (OE_latched, WE_latched);
endmodule

module rt2 (
  input  [15:0] in,
  input  [2:0] shamt,
  output [15:0] out
);

  wire multiplexer_1_out, multiplexer_2_out, multiplexer_3_out, multiplexer_4_out, multiplexer_7_out,
       multiplexer_8_out, multiplexer_10_out, multiplexer_11_out, multiplexer_12_out, multiplexer_13_out,
       multiplexer_16_out, multiplexer_17_out, multiplexer_19_out, multiplexer_20_out, multiplexer_21_out,
       multiplexer_22_out, multiplexer_25_out, multiplexer_26_out, multiplexer_27_out, multiplexer_28_out,
       multiplexer_31_out, multiplexer_32_out, multiplexer_34_out, multiplexer_35_out, multiplexer_36_out,
       multiplexer_37_out, multiplexer_40_out, multiplexer_41_out, multiplexer_43_out, multiplexer_44_out,
       multiplexer_45_out, multiplexer_46_out, not_1_out, not_2_out, not_3_out;

  not not_1 (not_1_out, shamt[0]);
  not not_2 (not_2_out, shamt[1]);
  not not_3 (not_3_out, shamt[2]);
  Multiplexer #(.enable("false")) multiplexer_1 (.in0(in[15]), .in1(in[14]), .out(multiplexer_1_out), .sel(not_1_out));
  Multiplexer #(.enable("false")) multiplexer_2 (.in0(in[15]), .in1(in[15]), .out(multiplexer_2_out), .sel(not_1_out));
  Multiplexer #(.enable("false")) multiplexer_3 (
    .in0(multiplexer_2_out), .in1(multiplexer_2_out), .out(multiplexer_3_out), .sel(not_2_out));
  Multiplexer #(.enable("false")) multiplexer_4 (
    .in0(multiplexer_1_out), .in1(multiplexer_1_out), .out(multiplexer_4_out), .sel(not_2_out));
  Multiplexer #(.enable("false")) multiplexer_5 (
    .in0(multiplexer_4_out), .in1(multiplexer_4_out), .out(out[14]), .sel(not_3_out));
  Multiplexer #(.enable("false")) multiplexer_6 (
    .in0(multiplexer_3_out), .in1(multiplexer_3_out), .out(out[15]), .sel(not_3_out));
  Multiplexer #(.enable("false")) multiplexer_7 (.in0(in[14]), .in1(in[13]), .out(multiplexer_7_out), .sel(not_1_out));
  Multiplexer #(.enable("false")) multiplexer_8 (
    .in0(multiplexer_2_out), .in1(multiplexer_7_out), .out(multiplexer_8_out), .sel(not_2_out));
  Multiplexer #(.enable("false")) multiplexer_9 (
    .in0(multiplexer_8_out), .in1(multiplexer_8_out), .out(out[13]), .sel(not_3_out));
  Multiplexer #(.enable("false")) multiplexer_10 (
    .in0(in[13]), .in1(in[12]), .out(multiplexer_10_out), .sel(not_1_out));
  Multiplexer #(.enable("false")) multiplexer_11 (
    .in0(in[12]), .in1(in[11]), .out(multiplexer_11_out), .sel(not_1_out));
  Multiplexer #(.enable("false")) multiplexer_12 (
    .in0(multiplexer_7_out), .in1(multiplexer_11_out), .out(multiplexer_12_out), .sel(not_2_out));
  Multiplexer #(.enable("false")) multiplexer_13 (
    .in0(multiplexer_1_out), .in1(multiplexer_10_out), .out(multiplexer_13_out), .sel(not_2_out));
  Multiplexer #(.enable("false")) multiplexer_14 (
    .in0(multiplexer_3_out), .in1(multiplexer_12_out), .out(out[11]), .sel(not_3_out));
  Multiplexer #(.enable("false")) multiplexer_15 (
    .in0(multiplexer_13_out), .in1(multiplexer_13_out), .out(out[12]), .sel(not_3_out));
  Multiplexer #(.enable("false")) multiplexer_16 (
    .in0(in[11]), .in1(in[10]), .out(multiplexer_16_out), .sel(not_1_out));
  Multiplexer #(.enable("false")) multiplexer_17 (
    .in0(multiplexer_10_out), .in1(multiplexer_16_out), .out(multiplexer_17_out), .sel(not_2_out));
  Multiplexer #(.enable("false")) multiplexer_18 (
    .in0(multiplexer_4_out), .in1(multiplexer_17_out), .out(out[10]), .sel(not_3_out));
  Multiplexer #(.enable("false")) multiplexer_19 (.in0(in[9]), .in1(in[8]), .out(multiplexer_19_out), .sel(not_1_out));
  Multiplexer #(.enable("false")) multiplexer_20 (.in0(in[10]), .in1(in[9]), .out(multiplexer_20_out), .sel(not_1_out));
  Multiplexer #(.enable("false")) multiplexer_21 (
    .in0(multiplexer_16_out), .in1(multiplexer_19_out), .out(multiplexer_21_out), .sel(not_2_out));
  Multiplexer #(.enable("false")) multiplexer_22 (
    .in0(multiplexer_11_out), .in1(multiplexer_20_out), .out(multiplexer_22_out), .sel(not_2_out));
  Multiplexer #(.enable("false")) multiplexer_23 (
    .in0(multiplexer_8_out), .in1(multiplexer_22_out), .out(out[9]), .sel(not_3_out));
  Multiplexer #(.enable("false")) multiplexer_24 (
    .in0(multiplexer_13_out), .in1(multiplexer_21_out), .out(out[8]), .sel(not_3_out));
  Multiplexer #(.enable("false")) multiplexer_25 (.in0(in[7]), .in1(in[6]), .out(multiplexer_25_out), .sel(not_1_out));
  Multiplexer #(.enable("false")) multiplexer_26 (.in0(in[8]), .in1(in[7]), .out(multiplexer_26_out), .sel(not_1_out));
  Multiplexer #(.enable("false")) multiplexer_27 (
    .in0(multiplexer_20_out), .in1(multiplexer_26_out), .out(multiplexer_27_out), .sel(not_2_out));
  Multiplexer #(.enable("false")) multiplexer_28 (
    .in0(multiplexer_19_out), .in1(multiplexer_25_out), .out(multiplexer_28_out), .sel(not_2_out));
  Multiplexer #(.enable("false")) multiplexer_29 (
    .in0(multiplexer_12_out), .in1(multiplexer_27_out), .out(out[7]), .sel(not_3_out));
  Multiplexer #(.enable("false")) multiplexer_30 (
    .in0(multiplexer_17_out), .in1(multiplexer_28_out), .out(out[6]), .sel(not_3_out));
  Multiplexer #(.enable("false")) multiplexer_31 (.in0(in[6]), .in1(in[5]), .out(multiplexer_31_out), .sel(not_1_out));
  Multiplexer #(.enable("false")) multiplexer_32 (
    .in0(multiplexer_26_out), .in1(multiplexer_31_out), .out(multiplexer_32_out), .sel(not_2_out));
  Multiplexer #(.enable("false")) multiplexer_33 (
    .in0(multiplexer_22_out), .in1(multiplexer_32_out), .out(out[5]), .sel(not_3_out));
  Multiplexer #(.enable("false")) multiplexer_34 (.in0(in[4]), .in1(in[3]), .out(multiplexer_34_out), .sel(not_1_out));
  Multiplexer #(.enable("false")) multiplexer_35 (.in0(in[5]), .in1(in[4]), .out(multiplexer_35_out), .sel(not_1_out));
  Multiplexer #(.enable("false")) multiplexer_36 (
    .in0(multiplexer_25_out), .in1(multiplexer_35_out), .out(multiplexer_36_out), .sel(not_2_out));
  Multiplexer #(.enable("false")) multiplexer_37 (
    .in0(multiplexer_31_out), .in1(multiplexer_34_out), .out(multiplexer_37_out), .sel(not_2_out));
  Multiplexer #(.enable("false")) multiplexer_38 (
    .in0(multiplexer_21_out), .in1(multiplexer_36_out), .out(out[4]), .sel(not_3_out));
  Multiplexer #(.enable("false")) multiplexer_39 (
    .in0(multiplexer_27_out), .in1(multiplexer_37_out), .out(out[3]), .sel(not_3_out));
  Multiplexer #(.enable("false")) multiplexer_40 (.in0(in[3]), .in1(in[2]), .out(multiplexer_40_out), .sel(not_1_out));
  Multiplexer #(.enable("false")) multiplexer_41 (
    .in0(multiplexer_35_out), .in1(multiplexer_40_out), .out(multiplexer_41_out), .sel(not_2_out));
  Multiplexer #(.enable("false")) multiplexer_42 (
    .in0(multiplexer_28_out), .in1(multiplexer_41_out), .out(out[2]), .sel(not_3_out));
  Multiplexer #(.enable("false")) multiplexer_43 (.in0(in[2]), .in1(in[1]), .out(multiplexer_43_out), .sel(not_1_out));
  Multiplexer #(.enable("false")) multiplexer_44 (.in0(in[1]), .in1(in[0]), .out(multiplexer_44_out), .sel(not_1_out));
  Multiplexer #(.enable("false")) multiplexer_45 (
    .in0(multiplexer_40_out), .in1(multiplexer_44_out), .out(multiplexer_45_out), .sel(not_2_out));
  Multiplexer #(.enable("false")) multiplexer_46 (
    .in0(multiplexer_34_out), .in1(multiplexer_43_out), .out(multiplexer_46_out), .sel(not_2_out));
  Multiplexer #(.enable("false")) multiplexer_47 (
    .in0(multiplexer_36_out), .in1(multiplexer_45_out), .out(out[0]), .sel(not_3_out));
  Multiplexer #(.enable("false")) multiplexer_48 (
    .in0(multiplexer_32_out), .in1(multiplexer_46_out), .out(out[1]), .sel(not_3_out));

  // Other names for the same wires on the sheet: shift = shamt[0]; sh1 = shamt[1]; sh2 = shamt[2]
endmodule

module backuprt (
  input  [15:0] in,
  input  [2:0] shamt,
  output [15:0] out
);

  wire multiplexer_1_out, multiplexer_2_out, multiplexer_3_out, multiplexer_4_out, multiplexer_5_out,
       multiplexer_6_out, multiplexer_7_out, multiplexer_8_out, multiplexer_9_out, multiplexer_10_out,
       multiplexer_11_out, multiplexer_12_out, multiplexer_13_out, multiplexer_14_out, multiplexer_15_out,
       multiplexer_16_out, multiplexer_17_out, multiplexer_18_out, multiplexer_19_out, multiplexer_20_out,
       multiplexer_21_out, multiplexer_22_out, multiplexer_23_out, multiplexer_24_out, multiplexer_25_out,
       multiplexer_26_out, multiplexer_27_out, multiplexer_28_out, multiplexer_30_out, multiplexer_31_out,
       multiplexer_34_out, multiplexer_35_out;

  Multiplexer #(.enable("false")) multiplexer_1 (.in0(in[0]), .in1(in[1]), .out(multiplexer_1_out), .sel(shamt[0]));
  Multiplexer #(.enable("false")) multiplexer_2 (.in0(in[1]), .in1(in[2]), .out(multiplexer_2_out), .sel(shamt[0]));
  Multiplexer #(.enable("false")) multiplexer_3 (.in0(in[2]), .in1(in[3]), .out(multiplexer_3_out), .sel(shamt[0]));
  Multiplexer #(.enable("false")) multiplexer_4 (.in0(in[3]), .in1(in[4]), .out(multiplexer_4_out), .sel(shamt[0]));
  Multiplexer #(.enable("false")) multiplexer_5 (.in0(in[4]), .in1(in[5]), .out(multiplexer_5_out), .sel(shamt[0]));
  Multiplexer #(.enable("false")) multiplexer_6 (.in0(in[5]), .in1(in[6]), .out(multiplexer_6_out), .sel(shamt[0]));
  Multiplexer #(.enable("false")) multiplexer_7 (.in0(in[6]), .in1(in[7]), .out(multiplexer_7_out), .sel(shamt[0]));
  Multiplexer #(.enable("false")) multiplexer_8 (.in0(in[7]), .in1(in[8]), .out(multiplexer_8_out), .sel(shamt[0]));
  Multiplexer #(.enable("false")) multiplexer_9 (.in0(in[8]), .in1(in[9]), .out(multiplexer_9_out), .sel(shamt[0]));
  Multiplexer #(.enable("false")) multiplexer_10 (.in0(in[9]), .in1(in[10]), .out(multiplexer_10_out), .sel(shamt[0]));
  Multiplexer #(.enable("false")) multiplexer_11 (.in0(in[10]), .in1(in[11]), .out(multiplexer_11_out), .sel(shamt[0]));
  Multiplexer #(.enable("false")) multiplexer_12 (.in0(in[11]), .in1(in[12]), .out(multiplexer_12_out), .sel(shamt[0]));
  Multiplexer #(.enable("false")) multiplexer_13 (.in0(in[12]), .in1(in[13]), .out(multiplexer_13_out), .sel(shamt[0]));
  Multiplexer #(.enable("false")) multiplexer_14 (.in0(in[13]), .in1(in[14]), .out(multiplexer_14_out), .sel(shamt[0]));
  Multiplexer #(.enable("false")) multiplexer_15 (.in0(in[14]), .in1(in[15]), .out(multiplexer_15_out), .sel(shamt[0]));
  Multiplexer #(.enable("false")) multiplexer_16 (.in0(in[15]), .in1(in[15]), .out(multiplexer_16_out), .sel(shamt[0]));
  Multiplexer #(.enable("false")) multiplexer_17 (
    .in0(multiplexer_1_out), .in1(multiplexer_3_out), .out(multiplexer_17_out), .sel(shamt[1]));
  Multiplexer #(.enable("false")) multiplexer_18 (
    .in0(multiplexer_2_out), .in1(multiplexer_4_out), .out(multiplexer_18_out), .sel(shamt[1]));
  Multiplexer #(.enable("false")) multiplexer_19 (
    .in0(multiplexer_3_out), .in1(multiplexer_5_out), .out(multiplexer_19_out), .sel(shamt[1]));
  Multiplexer #(.enable("false")) multiplexer_20 (
    .in0(multiplexer_4_out), .in1(multiplexer_6_out), .out(multiplexer_20_out), .sel(shamt[1]));
  Multiplexer #(.enable("false")) multiplexer_21 (
    .in0(multiplexer_5_out), .in1(multiplexer_7_out), .out(multiplexer_21_out), .sel(shamt[1]));
  Multiplexer #(.enable("false")) multiplexer_22 (
    .in0(multiplexer_6_out), .in1(multiplexer_8_out), .out(multiplexer_22_out), .sel(shamt[1]));
  Multiplexer #(.enable("false")) multiplexer_23 (
    .in0(multiplexer_7_out), .in1(multiplexer_9_out), .out(multiplexer_23_out), .sel(shamt[1]));
  Multiplexer #(.enable("false")) multiplexer_24 (
    .in0(multiplexer_8_out), .in1(multiplexer_10_out), .out(multiplexer_24_out), .sel(shamt[1]));
  Multiplexer #(.enable("false")) multiplexer_25 (
    .in0(multiplexer_9_out), .in1(multiplexer_11_out), .out(multiplexer_25_out), .sel(shamt[1]));
  Multiplexer #(.enable("false")) multiplexer_26 (
    .in0(multiplexer_10_out), .in1(multiplexer_12_out), .out(multiplexer_26_out), .sel(shamt[1]));
  Multiplexer #(.enable("false")) multiplexer_27 (
    .in0(multiplexer_11_out), .in1(multiplexer_13_out), .out(multiplexer_27_out), .sel(shamt[1]));
  Multiplexer #(.enable("false")) multiplexer_28 (
    .in0(multiplexer_12_out), .in1(multiplexer_14_out), .out(multiplexer_28_out), .sel(shamt[1]));
  Multiplexer #(.enable("false")) multiplexer_29 (
    .in0(multiplexer_17_out), .in1(multiplexer_21_out), .out(out[2]), .sel(shamt[2]));
  Multiplexer #(.enable("false")) multiplexer_30 (
    .in0(multiplexer_13_out), .in1(multiplexer_15_out), .out(multiplexer_30_out), .sel(shamt[1]));
  Multiplexer #(.enable("false")) multiplexer_31 (
    .in0(multiplexer_14_out), .in1(multiplexer_16_out), .out(multiplexer_31_out), .sel(shamt[1]));
  Multiplexer #(.enable("false")) multiplexer_32 (
    .in0(multiplexer_18_out), .in1(multiplexer_22_out), .out(out[1]), .sel(shamt[2]));
  Multiplexer #(.enable("false")) multiplexer_33 (
    .in0(multiplexer_19_out), .in1(multiplexer_23_out), .out(out[0]), .sel(shamt[2]));
  Multiplexer #(.enable("false")) multiplexer_34 (
    .in0(multiplexer_15_out), .in1(in[15]), .out(multiplexer_34_out), .sel(shamt[1]));
  Multiplexer #(.enable("false")) multiplexer_35 (
    .in0(multiplexer_16_out), .in1(in[15]), .out(multiplexer_35_out), .sel(shamt[1]));
  Multiplexer #(.enable("false")) multiplexer_36 (
    .in0(multiplexer_20_out), .in1(multiplexer_24_out), .out(out[3]), .sel(shamt[2]));
  Multiplexer #(.enable("false")) multiplexer_37 (
    .in0(multiplexer_21_out), .in1(multiplexer_25_out), .out(out[4]), .sel(shamt[2]));
  Multiplexer #(.enable("false")) multiplexer_38 (
    .in0(multiplexer_22_out), .in1(multiplexer_26_out), .out(out[5]), .sel(shamt[2]));
  Multiplexer #(.enable("false")) multiplexer_39 (
    .in0(multiplexer_23_out), .in1(multiplexer_27_out), .out(out[6]), .sel(shamt[2]));
  Multiplexer #(.enable("false")) multiplexer_40 (
    .in0(multiplexer_24_out), .in1(multiplexer_28_out), .out(out[7]), .sel(shamt[2]));
  Multiplexer #(.enable("false")) multiplexer_41 (
    .in0(multiplexer_25_out), .in1(multiplexer_30_out), .out(out[8]), .sel(shamt[2]));
  Multiplexer #(.enable("false")) multiplexer_42 (
    .in0(multiplexer_26_out), .in1(multiplexer_31_out), .out(out[9]), .sel(shamt[2]));
  Multiplexer #(.enable("false")) multiplexer_43 (
    .in0(multiplexer_27_out), .in1(multiplexer_34_out), .out(out[10]), .sel(shamt[2]));
  Multiplexer #(.enable("false")) multiplexer_44 (
    .in0(multiplexer_28_out), .in1(multiplexer_35_out), .out(out[11]), .sel(shamt[2]));
  Multiplexer #(.enable("false")) multiplexer_45 (
    .in0(multiplexer_30_out), .in1(in[15]), .out(out[12]), .sel(shamt[2]));
  Multiplexer #(.enable("false")) multiplexer_46 (
    .in0(multiplexer_31_out), .in1(in[15]), .out(out[13]), .sel(shamt[2]));
  Multiplexer #(.enable("false")) multiplexer_47 (
    .in0(multiplexer_34_out), .in1(in[15]), .out(out[14]), .sel(shamt[2]));
  Multiplexer #(.enable("false")) multiplexer_48 (
    .in0(multiplexer_35_out), .in1(in[15]), .out(out[15]), .sel(shamt[2]));

  // Other names for the same wires on the sheet: shift = shamt[0]; sh1 = shamt[1]; sh2 = shamt[2]
endmodule

module PCreg (
  input  [15:0] data_in,
  input  clk,
  input  write_enable,
  input  reset,
  output [15:0] data_out
);

  wire and_1_out;

  and and_1 (and_1_out, clk, write_enable);
  D_Flip_Flop d_ff_1 (.D(data_in[0]), .clk(and_1_out), .Q(data_out[0]), .reset(reset));  // open: Qn, preset
  D_Flip_Flop d_ff_2 (.D(data_in[1]), .clk(and_1_out), .Q(data_out[1]), .reset(reset));  // open: Qn, preset
  D_Flip_Flop d_ff_3 (.D(data_in[2]), .clk(and_1_out), .Q(data_out[2]), .reset(reset));  // open: Qn, preset
  D_Flip_Flop d_ff_4 (.D(data_in[3]), .clk(and_1_out), .Q(data_out[3]), .reset(reset));  // open: Qn, preset
  D_Flip_Flop d_ff_5 (.D(data_in[4]), .clk(and_1_out), .Q(data_out[4]), .reset(reset));  // open: Qn, preset
  D_Flip_Flop d_ff_6 (.D(data_in[5]), .clk(and_1_out), .Q(data_out[5]), .reset(reset));  // open: Qn, preset
  D_Flip_Flop d_ff_7 (.D(data_in[6]), .clk(and_1_out), .Q(data_out[6]), .reset(reset));  // open: Qn, preset
  D_Flip_Flop d_ff_8 (.D(data_in[7]), .clk(and_1_out), .Q(data_out[7]), .reset(reset));  // open: Qn, preset
  D_Flip_Flop d_ff_9 (.D(data_in[8]), .clk(and_1_out), .Q(data_out[8]), .reset(reset));  // open: Qn, preset
  D_Flip_Flop d_ff_10 (.D(data_in[9]), .clk(and_1_out), .Q(data_out[9]), .reset(reset));  // open: Qn, preset
  D_Flip_Flop d_ff_11 (.D(data_in[10]), .clk(and_1_out), .Q(data_out[10]), .reset(reset));  // open: Qn, preset
  D_Flip_Flop d_ff_12 (.D(data_in[11]), .clk(and_1_out), .Q(data_out[11]), .reset(reset));  // open: Qn, preset
  D_Flip_Flop d_ff_13 (.D(data_in[12]), .clk(and_1_out), .Q(data_out[12]), .reset(reset));  // open: Qn, preset
  D_Flip_Flop d_ff_14 (.D(data_in[13]), .clk(and_1_out), .Q(data_out[13]), .reset(reset));  // open: Qn, preset
  D_Flip_Flop d_ff_15 (.D(data_in[14]), .clk(and_1_out), .Q(data_out[14]), .reset(reset));  // open: Qn, preset
  D_Flip_Flop d_ff_16 (.D(data_in[15]), .clk(and_1_out), .Q(data_out[15]), .reset(reset));  // open: Qn, preset
endmodule
